# Fritzing sketch 2024-02-04 Vaus Gaming paddle shematic v0.01 (saved by Fritzing 1.0.2b)
circuit board: 10.4669cm x 5.73075cm
perfboards: 1

parts:
  S1 = Round Pushbutton
  Arduino_Micro = Arduino Micro (Rev3)
  U1_=_20_leds_WS2812B_144led/m = WS2812 RGB LED strip
  U2_=_20_leds_WS2812B_144led/m = WS2812 RGB LED strip
  U3_=_17_leds_WS2812B_144led/m = WS2812 RGB LED strip
  R1_(128mm_smooth_fader_linear) = Slide Potentiometer [maximum_resistance=10kΩ knob_status=50% power=0.5W package=THT]
  R2 = 6mm Trimmer Potentiometer [maximum_resistance=100kΩ knob_status=50% power=0.5W package=THT]
  C1 = Electrolytic Capacitor [capacitance=10µF voltage=63V package="100 mil [THT, electrolytic]"]
  LED1 = LED - 5mm [color="Red (633nm)" current=0.030A package="5 mm [THT]"]
  R3 = Resistor [tolerance=±5% power=0.25W resistance=1000 package=THT]
  J2 = female pin header, 3 pins [form="♀ (female)"]

nets:
  GND: S1.leg0, Arduino_Micro.GND, U1_=_20_leds_WS2812B_144led/m.GND#0, R1_(128mm_smooth_fader_linear).leg1, R2.leg1, C1.-, LED1.cathode, J2.pin3
  N1: S1.leg1, Arduino_Micro.D2/SDA
  N2: Arduino_Micro.D5_PWM, U1_=_20_leds_WS2812B_144led/m.DIN, J2.pin2
  5V: Arduino_Micro.5V, U1_=_20_leds_WS2812B_144led/m.VCC#1, R3.Pin_0, J2.pin1
  N3: Arduino_Micro.A1, R2.wiper
  N4: Arduino_Micro.A0, R1_(128mm_smooth_fader_linear).wiper, C1.+
  N5: Arduino_Micro.AREF, R1_(128mm_smooth_fader_linear).leg2, R2.leg2
  N6: U1_=_20_leds_WS2812B_144led/m.GND#4, U2_=_20_leds_WS2812B_144led/m.GND#0
  N7: U1_=_20_leds_WS2812B_144led/m.VCC#5, U2_=_20_leds_WS2812B_144led/m.VCC#1
  N8: U1_=_20_leds_WS2812B_144led/m.DOUT, U2_=_20_leds_WS2812B_144led/m.DIN
  N9: U2_=_20_leds_WS2812B_144led/m.GND#4, U3_=_17_leds_WS2812B_144led/m.GND
  N10: U2_=_20_leds_WS2812B_144led/m.VCC#5, U3_=_17_leds_WS2812B_144led/m.VCC
  N11: U2_=_20_leds_WS2812B_144led/m.DOUT, U3_=_17_leds_WS2812B_144led/m.DIN
  N12: LED1.anode, R3.Pin_1

notes:
  Vaus gaming paddle for Arkanoid 1 and 2
  Hippolyte Mounier
  2024.02.04
  Vaus Gaming Paddle by Hippolyte Mounier

custom parts:
  WS2812 RGB LED strip: WS2812 strip
