# Fritzing sketch 2024-09-23 Vaus Gaming paddle shematic v1.02 (saved by Fritzing 1.0.2b)
circuit board: 8.9967cm x 4.56103cm
perfboards: 1

parts:
  Fire_button = Round Pushbutton
  Arduino_Micro = Arduino Micro (Rev3)
  U1_=_20_leds_WS2812B_144led/m = WS2812 RGB LED strip
  U2_=_20_leds_WS2812B_144led/m = WS2812 RGB LED strip
  U3_=_17_leds_WS2812B_144led/m = WS2812 RGB LED strip
  R1_(128mm_smooth_fader_linear) = Slide Potentiometer [maximum_resistance=10kΩ knob_status=50% power=0.5W package=THT]
  Sensitivity_Pot = 6mm Trimmer Potentiometer [maximum_resistance=100kΩ knob_status=50% power=0.5W package=THT]
  C1 = Electrolytic Capacitor [capacitance=10µF voltage=63V package="100 mil [THT, electrolytic]"]
  LED1 = LED - 5mm [color="Red (633nm)" current=0.030A package="5 mm [THT]"]
  R3 = Resistor [tolerance=±5% power=0.25W resistance=1000 package=THT]
  J2 = female pin header, 3 pins [form="♀ (female)"]

nets:
  GND: Fire_button.leg0, Arduino_Micro.GND, U1_=_20_leds_WS2812B_144led/m.GND#0, R1_(128mm_smooth_fader_linear).leg1, Sensitivity_Pot.leg1, C1.-, LED1.cathode, J2.pin3
  N1: Fire_button.leg1, Arduino_Micro.D2/SDA
  LED strip data out: Arduino_Micro.D5_PWM, U1_=_20_leds_WS2812B_144led/m.DIN, J2.pin2
  5V: Arduino_Micro.5V, U1_=_20_leds_WS2812B_144led/m.VCC#1, R3.Pin_0, J2.pin1
  V Sensitivity pot: Arduino_Micro.A1, Sensitivity_Pot.wiper
  V Paddle: Arduino_Micro.A0, R1_(128mm_smooth_fader_linear).wiper, C1.+
  VCC Analog: Arduino_Micro.AREF, R1_(128mm_smooth_fader_linear).leg2, Sensitivity_Pot.leg2
  N2: U1_=_20_leds_WS2812B_144led/m.GND#4, U2_=_20_leds_WS2812B_144led/m.GND#0
  N3: U1_=_20_leds_WS2812B_144led/m.VCC#5, U2_=_20_leds_WS2812B_144led/m.VCC#1
  N4: U1_=_20_leds_WS2812B_144led/m.DOUT, U2_=_20_leds_WS2812B_144led/m.DIN
  N5: U2_=_20_leds_WS2812B_144led/m.GND#4, U3_=_17_leds_WS2812B_144led/m.GND
  N6: U2_=_20_leds_WS2812B_144led/m.VCC#5, U3_=_17_leds_WS2812B_144led/m.VCC
  N7: U2_=_20_leds_WS2812B_144led/m.DOUT, U3_=_17_leds_WS2812B_144led/m.DIN
  N8: LED1.anode, R3.Pin_1

notes:
  Vaus gaming paddle for Arkanoid 1 and 2
  Hippolyte Mounier
  2024.09.23
  by Hippo, Vaus Gaming Paddle shematic
  LED strip shematic
  LED shematic
  Paddle potentiometer wiring
  Sensitivity potentiometer wiring
  VAUS gaming paddle
  by Hippo
  black wire side
  PCB v1.00

custom parts:
  WS2812 RGB LED strip: WS2812 strip
